// Logisim project cpu.circ as structural Verilog: 4 circuits, main circuit m
module m (
  input  [15:0] in_1,
  input  in_2,
  input  rOE,
  input  OPEnable,
  output [7:0] out_5,
  output [7:0] out_6,
  output [15:0] out_7,
  output [15:0] out_8,
  output [15:0] out_9,
  output [15:0] out_10,
  output out_11,
  output [15:0] out_12,
  output [15:0] out_13
);

  wire alu_1_rdout, clock_1_out, cui_1_c0, cui_1_c1, cui_1_c2, cui_1_c3, cui_1_c4, cui_1_c5, cui_1_c6,
       cui_1_c7, cui_1_c8, cui_1_c9, cui_1_c10, cui_1_c11, cui_1_c12, cui_1_c13, cui_1_c14, cui_1_c15,
       seven_segment_display_1_neg, seven_segment_display_2_neg, seven_segment_display_3_neg,
       seven_segment_display_5_neg;
  wire [2:0] counter_2_q;
  wire [3:0] bitselector_2_out, n7_segment_display_2_p1, n7_segment_display_2_p2, n7_segment_display_4_p1,
       n7_segment_display_4_p2, n7_segment_display_6_p1, n7_segment_display_6_p2, n7_segment_display_7_p2,
       n7_segment_display_8_p2, n7_segment_display_9_p2, n7_segment_display_21_p1, n7_segment_display_21_p2,
       n7_segment_display_22_p2, n7_segment_display_23_p2, seven_segment_display_1_out_7,
       seven_segment_display_1_tenth_place, seven_segment_display_2_out_7,
       seven_segment_display_2_tenth_place, seven_segment_display_3_out_7,
       seven_segment_display_3_tenth_place, seven_segment_display_4_out_7, seven_segment_display_5_out_7,
       seven_segment_display_6_out_7;
  wire [7:0] bitselector_1_out, eight_bit_register_1_dout;
  wire [15:0] alu_1_adout, bit_extender_1_out, bit_extender_3_out, ram_1_dout, sixteen_bit_register_1_out_6;

  // BCD_to_7_Segment_decoder bcd_to_7_segment_decoder_1: pin names not known
  _7_Segment_Display u_7_segment_display_1 (.g(seven_segment_display_1_neg));  // open: f, a, b, e, d, c, dp
  // _7_Segment_Display 7_segment_display_2: pin names not known; wires that end beside it: n7_segment_display_2_p1, n7_segment_display_2_p2
  // BCD_to_7_Segment_decoder bcd_to_7_segment_decoder_2: pin names not known
  _7_Segment_Display u_7_segment_display_3 (.g(seven_segment_display_2_neg));  // open: f, a, b, e, d, c, dp
  // _7_Segment_Display 7_segment_display_4: pin names not known; wires that end beside it: n7_segment_display_4_p1, n7_segment_display_4_p2
  // BCD_to_7_Segment_decoder bcd_to_7_segment_decoder_3: pin names not known
  _7_Segment_Display u_7_segment_display_5 (.g(seven_segment_display_3_neg));  // open: f, a, b, e, d, c, dp
  // _7_Segment_Display 7_segment_display_6: pin names not known; wires that end beside it: n7_segment_display_6_p1, n7_segment_display_6_p2
  // BCD_to_7_Segment_decoder bcd_to_7_segment_decoder_4: pin names not known
  // _7_Segment_Display 7_segment_display_7: pin names not known; wires that end beside it: n7_segment_display_2_p2, n7_segment_display_7_p2
  seven_segment_display seven_segment_display_1 (
    .Din(out_9), .tenth_place(seven_segment_display_1_tenth_place), .out_7(seven_segment_display_1_out_7),
    .neg(seven_segment_display_1_neg), .ten_thousand_place(n7_segment_display_2_p1),
    .thousand_place(n7_segment_display_2_p2), .hundreth_place(n7_segment_display_7_p2));
  // BCD_to_7_Segment_decoder bcd_to_7_segment_decoder_5: pin names not known
  // _7_Segment_Display 7_segment_display_8: pin names not known; wires that end beside it: n7_segment_display_4_p2, n7_segment_display_8_p2
  seven_segment_display seven_segment_display_2 (
    .Din(out_10), .tenth_place(seven_segment_display_2_tenth_place), .out_7(seven_segment_display_2_out_7),
    .neg(seven_segment_display_2_neg), .ten_thousand_place(n7_segment_display_4_p1),
    .thousand_place(n7_segment_display_4_p2), .hundreth_place(n7_segment_display_8_p2));
  // BCD_to_7_Segment_decoder bcd_to_7_segment_decoder_6: pin names not known
  // _7_Segment_Display 7_segment_display_9: pin names not known; wires that end beside it: n7_segment_display_6_p2, n7_segment_display_9_p2
  seven_segment_display seven_segment_display_3 (
    .Din(out_13), .tenth_place(seven_segment_display_3_tenth_place), .out_7(seven_segment_display_3_out_7),
    .neg(seven_segment_display_3_neg), .ten_thousand_place(n7_segment_display_6_p1),
    .thousand_place(n7_segment_display_6_p2), .hundreth_place(n7_segment_display_9_p2));
  // BCD_to_7_Segment_decoder bcd_to_7_segment_decoder_7: pin names not known
  // BCD_to_7_Segment_decoder bcd_to_7_segment_decoder_8: pin names not known
  // _7_Segment_Display 7_segment_display_10: pin names not known; wires that end beside it: n7_segment_display_7_p2, seven_segment_display_1_tenth_place
  // _7_Segment_Display 7_segment_display_11: pin names not known; wires that end beside it: seven_segment_display_1_tenth_place, seven_segment_display_1_out_7
  // BCD_to_7_Segment_decoder bcd_to_7_segment_decoder_9: pin names not known
  // BCD_to_7_Segment_decoder bcd_to_7_segment_decoder_10: pin names not known
  // _7_Segment_Display 7_segment_display_12: pin names not known; wires that end beside it: n7_segment_display_8_p2, seven_segment_display_2_tenth_place
  // _7_Segment_Display 7_segment_display_13: pin names not known; wires that end beside it: seven_segment_display_2_tenth_place, seven_segment_display_2_out_7
  // BCD_to_7_Segment_decoder bcd_to_7_segment_decoder_11: pin names not known
  // BCD_to_7_Segment_decoder bcd_to_7_segment_decoder_12: pin names not known
  // _7_Segment_Display 7_segment_display_14: pin names not known; wires that end beside it: n7_segment_display_9_p2, seven_segment_display_3_tenth_place
  // _7_Segment_Display 7_segment_display_15: pin names not known; wires that end beside it: seven_segment_display_3_tenth_place, seven_segment_display_3_out_7
  // BCD_to_7_Segment_decoder bcd_to_7_segment_decoder_13: pin names not known
  _7_Segment_Display u_7_segment_display_16 ();  // open: g, f, a, b, e, d, c, dp
  // BCD_to_7_Segment_decoder bcd_to_7_segment_decoder_14: pin names not known
  _7_Segment_Display u_7_segment_display_17 ();  // open: g, f, a, b, e, d, c, dp
  // BCD_to_7_Segment_decoder bcd_to_7_segment_decoder_15: pin names not known
  _7_Segment_Display u_7_segment_display_18 ();  // open: g, f, a, b, e, d, c, dp
  Clock clock_1 (.out(clock_1_out));
  seven_segment_display seven_segment_display_4 (
    .Din(bit_extender_1_out), .out_7(seven_segment_display_4_out_7));  // open: tenth_place, neg, ten_thousand_place, thousand_place, hundreth_place
  // BCD_to_7_Segment_decoder bcd_to_7_segment_decoder_16: pin names not known; wires that end beside it: seven_segment_display_4_out_7
  _7_Segment_Display u_7_segment_display_19 ();  // open: g, f, a, b, e, d, c, dp
  assign bit_extender_1_out = {{8{1'b0}}, out_6};  // Bit_Extender bit_extender_1
  Counter #(.max('h3)) counter_1 (
    .D(bitselector_1_out), .count(cui_1_c1), .Q(out_6), .clk(clock_1_out));  // open: load, carry, up, clr
  sixteen_bit_register sixteen_bit_register_1 (
    .in_1(alu_1_adout), .WE(cui_1_c7), .OE(cui_1_c8), .clock(clock_1_out),
    .out_6(sixteen_bit_register_1_out_6), .out_7(out_7));  // open: Reset
  sixteen_bit_register sixteen_bit_register_2 (
    .in_1(alu_1_adout), .WE(cui_1_c12), .clock(clock_1_out), .out_7(out_9));  // open: OE, Reset, out_6
  ALU alu_1 (
    .aOE(cui_1_c11), .rOE(rOE), .B(out_13), .A(out_9), .OPENABLE(OPEnable), .aDout(alu_1_adout),
    .AUoutput(out_10), .rDout(alu_1_rdout), .RUoutput(out_11));  // open: AUSel, RUsel
  sixteen_bit_register sixteen_bit_register_3 (
    .in_1(alu_1_adout), .WE(cui_1_c13), .clock(clock_1_out), .out_7(out_13));  // open: OE, Reset, out_6
  BitSelector #(.group(8), .width(16)) bitselector_1 (
    .in(sixteen_bit_register_1_out_6), .out(bitselector_1_out), .sel(1'b0));
  assign bitselector_1_out = cui_1_c0 ? out_6 : 8'bz;  // Controlled_Buffer controlled_buffer_1
  assign alu_1_adout = {{15{alu_1_rdout}}, alu_1_rdout};  // Bit_Extender bit_extender_2
  LED led_1 (.in(alu_1_adout[15]));
  LED led_2 (.in(alu_1_adout[14]));
  LED led_3 (.in(alu_1_adout[13]));
  LED led_4 (.in(alu_1_adout[12]));
  LED led_5 (.in(alu_1_adout[11]));
  LED led_6 (.in(alu_1_adout[10]));
  LED led_7 (.in(alu_1_adout[9]));
  LED led_8 (.in(alu_1_adout[8]));
  assign alu_1_adout = in_2 ? in_1 : 16'bz;  // Controlled_Buffer controlled_buffer_2
  LED led_9 (.in(alu_1_adout[7]));
  LED led_10 (.in(alu_1_adout[6]));
  LED led_11 (.in(alu_1_adout[5]));
  LED led_12 (.in(alu_1_adout[4]));
  LED led_13 (.in(alu_1_adout[3]));
  LED led_14 (.in(alu_1_adout[2]));
  LED led_15 (.in(alu_1_adout[1]));
  LED led_16 (.in(alu_1_adout[0]));
  assign alu_1_adout = cui_1_c5 ? out_8 : 16'bz;  // Controlled_Buffer controlled_buffer_3
  Eight_bit_register eight_bit_register_1 (
    .Din(bitselector_1_out), .OE(cui_1_c10), .clock(clock_1_out), .WE(cui_1_c9), .Stored_bit(out_5),
    .Dout(eight_bit_register_1_dout));  // open: reset
  sixteen_bit_register sixteen_bit_register_4 (
    .in_1(alu_1_adout), .WE(cui_1_c4), .OE(cui_1_c6), .clock(clock_1_out), .out_6(alu_1_adout), .out_7(out_8));  // open: Reset
  sixteen_bit_register sixteen_bit_register_5 (
    .in_1(alu_1_adout), .WE(cui_1_c15), .OE(cui_1_c14), .clock(clock_1_out), .out_6(alu_1_adout),
    .out_7(out_12));  // open: Reset
  LED led_17 (.in(alu_1_adout[15]));
  LED led_18 (.in(alu_1_adout[14]));
  // BCD_to_7_Segment_decoder bcd_to_7_segment_decoder_17: pin names not known
  _7_Segment_Display u_7_segment_display_20 (.g(seven_segment_display_5_neg));  // open: f, a, b, e, d, c, dp
  // _7_Segment_Display 7_segment_display_21: pin names not known; wires that end beside it: n7_segment_display_21_p1, n7_segment_display_21_p2
  LED led_19 (.in(alu_1_adout[13]));
  LED led_20 (.in(alu_1_adout[12]));
  LED led_21 (.in(alu_1_adout[11]));
  LED led_22 (.in(alu_1_adout[10]));
  // BCD_to_7_Segment_decoder bcd_to_7_segment_decoder_18: pin names not known
  // BCD_to_7_Segment_decoder bcd_to_7_segment_decoder_19: pin names not known
  // _7_Segment_Display 7_segment_display_22: pin names not known; wires that end beside it: n7_segment_display_21_p2, n7_segment_display_22_p2
  // _7_Segment_Display 7_segment_display_23: pin names not known; wires that end beside it: n7_segment_display_22_p2, n7_segment_display_23_p2
  seven_segment_display seven_segment_display_5 (
    .Din(out_12), .tenth_place(n7_segment_display_23_p2), .out_7(seven_segment_display_5_out_7),
    .neg(seven_segment_display_5_neg), .ten_thousand_place(n7_segment_display_21_p1),
    .thousand_place(n7_segment_display_21_p2), .hundreth_place(n7_segment_display_22_p2));
  LED led_23 (.in(alu_1_adout[9]));
  LED led_24 (.in(alu_1_adout[8]));
  LED led_25 (.in(alu_1_adout[7]));
  // BCD_to_7_Segment_decoder bcd_to_7_segment_decoder_20: pin names not known
  // _7_Segment_Display 7_segment_display_24: pin names not known; wires that end beside it: n7_segment_display_23_p2, seven_segment_display_5_out_7
  LED led_26 (.in(alu_1_adout[6]));
  LED led_27 (.in(alu_1_adout[5]));
  LED led_28 (.in(alu_1_adout[4]));
  LED led_29 (.in(alu_1_adout[3]));
  // BCD_to_7_Segment_decoder bcd_to_7_segment_decoder_21: pin names not known
  _7_Segment_Display u_7_segment_display_25 ();  // open: g, f, a, b, e, d, c, dp
  LED led_30 (.in(alu_1_adout[2]));
  LED led_31 (.in(alu_1_adout[1]));
  LED led_32 (.in(alu_1_adout[0]));
  RAM #(.dataWidth(16), .enables("line"), .\type ("nonvolatile")) ram_1 (
    .addr(eight_bit_register_1_dout), .we(cui_1_c2), .clk(clock_1_out), .dout(ram_1_dout));  // open: din
  assign alu_1_adout = cui_1_c3 ? ram_1_dout : 16'bz;  // Controlled_Buffer controlled_buffer_4
  Counter #(.max('h5), .width(3)) counter_2 (
    .Q(counter_2_q), .clk(clock_1_out));  // open: load, D, count, carry, up, clr
  BitSelector #(.group(4), .width(16)) bitselector_2 (.in(out_7), .out(bitselector_2_out), .sel(2'b01));
  seven_segment_display seven_segment_display_6 (
    .Din(bit_extender_3_out), .out_7(seven_segment_display_6_out_7));  // open: tenth_place, neg, ten_thousand_place, thousand_place, hundreth_place
  assign bit_extender_3_out = {{13{1'b0}}, counter_2_q};  // Bit_Extender bit_extender_3
  // BCD_to_7_Segment_decoder bcd_to_7_segment_decoder_22: pin names not known; wires that end beside it: seven_segment_display_6_out_7
  _7_Segment_Display u_7_segment_display_26 ();  // open: g, f, a, b, e, d, c, dp
  CUI cui_1 (
    .OPC3(bitselector_2_out[3]), .OPC2(bitselector_2_out[2]), .OPC1(bitselector_2_out[1]),
    .OPC0(bitselector_2_out[0]), .SC2(counter_2_q[2]), .SC1(counter_2_q[1]), .SC0(counter_2_q[0]),
    .C0(cui_1_c0), .C1(cui_1_c1), .C2(cui_1_c2), .C3(cui_1_c3), .C4(cui_1_c4), .C5(cui_1_c5), .C6(cui_1_c6),
    .C7(cui_1_c7), .C8(cui_1_c8), .C9(cui_1_c9), .C10(cui_1_c10), .C11(cui_1_c11), .C12(cui_1_c12),
    .C13(cui_1_c13), .C14(cui_1_c14), .C15(cui_1_c15));

  // Notes on the sheet:
  //   Register A
  //   Register B
  //   Instruction Register
endmodule

module CU (
  input  OPC3,
  input  OPC2,
  input  OPC1,
  input  OPC0,
  input  SC2,
  input  SC1,
  input  SC0,
  output C0,
  output C1,
  output C2,
  output C3,
  output C4,
  output C5,
  output C6,
  output C7,
  output C8,
  output C9,
  output C10,
  output C11,
  output C12,
  output C13,
  output C14,
  output C15
);

  wire and_4_out, and_5_out, and_6_out, and_7_out, and_8_out, and_9_out, and_10_out, and_13_out, and_14_out,
       and_15_out, and_16_out, and_17_out, and_18_out, and_19_out, not_1_out, not_2_out, not_3_out,
       not_4_out, not_5_out;

  not not_1 (not_1_out, OPC1);
  not not_2 (not_2_out, OPC0);
  not not_3 (not_3_out, SC2);
  not not_4 (not_4_out, SC1);
  not not_5 (not_5_out, SC0);
  and and_1 (C0, not_3_out, not_4_out, not_5_out);
  and and_2 (C1, not_3_out, not_4_out, SC0);
  and and_3 (C2, OPC1, SC2);
  and and_4 (and_4_out, not_3_out, not_4_out, SC0);
  and and_5 (and_5_out, not_1_out, SC2, not_5_out);
  and and_6 (and_6_out, not_3_out, not_4_out, SC0);
  and and_7 (and_7_out, OPC1, OPC0, SC0);
  and and_8 (and_8_out, not_1_out, SC2, not_5_out);
  and and_9 (and_9_out, SC1, not_5_out);
  and and_10 (and_10_out, SC2, SC0);
  and and_11 (C6, OPC1, SC2);
  and and_12 (C7, SC1, not_5_out);
  and and_13 (and_13_out, not_1_out, SC1, SC0);
  and and_14 (and_14_out, OPC0, SC1, SC0);
  and and_15 (and_15_out, not_3_out, not_4_out, not_5_out);
  and and_16 (and_16_out, not_1_out, SC1, SC0);
  and and_17 (and_17_out, OPC0, SC1, SC0);
  and and_18 (and_18_out, not_3_out, not_4_out, SC0);
  and and_19 (and_19_out, SC2, not_5_out);
  and and_20 (C11, OPC1, not_2_out, SC1, SC0);
  and and_21 (C12, not_2_out, SC2, SC0);
  and and_22 (C13, OPC0, SC2, SC0);
  and and_23 (C14, OPC1, OPC0, SC1, SC0);
  and and_24 (C15, OPC1, not_2_out, SC1, SC0);
  or or_1 (C3, and_4_out, and_5_out);
  or or_2 (C4, and_6_out, and_7_out, and_8_out);
  or or_3 (C5, and_9_out, and_10_out);
  or or_4 (C8, and_13_out, and_14_out);
  or or_5 (C9, and_15_out, and_16_out, and_17_out);
  or or_6 (C10, and_18_out, and_19_out);
endmodule

module try (
  input  [6:0] in_1,
  output [15:0] out_2
);

  CU cu_1 (
    .OPC3(in_1[0]), .OPC2(in_1[1]), .OPC1(in_1[2]), .OPC0(in_1[3]), .SC2(in_1[4]), .SC1(in_1[5]),
    .SC0(in_1[6]), .C0(out_2[0]), .C1(out_2[1]), .C2(out_2[2]), .C3(out_2[3]), .C4(out_2[4]), .C5(out_2[5]),
    .C6(out_2[6]), .C7(out_2[7]), .C8(out_2[8]), .C9(out_2[9]), .C10(out_2[10]), .C11(out_2[11]),
    .C12(out_2[12]), .C13(out_2[13]), .C14(out_2[14]), .C15(out_2[15]));
endmodule

module CUI (
  input  OPC3,
  input  OPC2,
  input  OPC1,
  input  OPC0,
  input  SC2,
  input  SC1,
  input  SC0,
  output C0,
  output C1,
  output C2,
  output C3,
  output C4,
  output C5,
  output C6,
  output C7,
  output C8,
  output C9,
  output C10,
  output C11,
  output C12,
  output C13,
  output C14,
  output C15
);

  wire and_4_out, and_5_out, and_6_out, and_7_out, and_8_out, and_9_out, and_10_out, and_13_out, and_14_out,
       and_15_out, and_16_out, and_17_out, and_18_out, and_19_out, not_1_out, not_2_out, not_3_out,
       not_4_out, not_5_out;

  not not_1 (not_1_out, OPC1);
  not not_2 (not_2_out, OPC0);
  not not_3 (not_3_out, SC2);
  not not_4 (not_4_out, SC1);
  not not_5 (not_5_out, SC0);
  and and_1 (C0, not_3_out, not_4_out, not_5_out);
  and and_2 (C1, not_3_out, not_4_out, SC0);
  and and_3 (C2, OPC1, SC2);
  and and_4 (and_4_out, not_3_out, not_4_out, SC0);
  and and_5 (and_5_out, not_1_out, SC2, not_5_out);
  and and_6 (and_6_out, not_3_out, not_4_out, SC0);
  and and_7 (and_7_out, OPC1, OPC0, SC0);
  and and_8 (and_8_out, not_1_out, SC2, not_5_out);
  and and_9 (and_9_out, SC1, not_5_out);
  and and_10 (and_10_out, SC2, SC0);
  and and_11 (C6, OPC1, SC2);
  and and_12 (C7, SC1, not_5_out);
  and and_13 (and_13_out, not_1_out, SC1, SC0);
  and and_14 (and_14_out, OPC0, SC1, SC0);
  and and_15 (and_15_out, not_3_out, not_4_out, not_5_out);
  and and_16 (and_16_out, not_1_out, SC1, SC0);
  and and_17 (and_17_out, OPC0, SC1, SC0);
  and and_18 (and_18_out, not_3_out, not_4_out, SC0);
  and and_19 (and_19_out, SC2, not_5_out);
  and and_20 (C11, OPC1, not_2_out, SC1, SC0);
  and and_21 (C12, not_2_out, SC2, SC0);
  and and_22 (C13, OPC0, SC2, SC0);
  and and_23 (C14, OPC1, OPC0, SC1, SC0);
  and and_24 (C15, OPC1, not_2_out, SC1, SC0);
  or or_1 (C3, and_4_out, and_5_out);
  or or_2 (C4, and_6_out, and_7_out, and_8_out);
  or or_3 (C5, and_9_out, and_10_out);
  or or_4 (C8, and_13_out, and_14_out);
  or or_5 (C9, and_15_out, and_16_out, and_17_out);
  or or_6 (C10, and_18_out, and_19_out);
endmodule
