// Logisim project Registers.circ as structural Verilog: 3 circuits, main circuit Eight_bit_register
module Eight_bit_register (
  input  [7:0] Din,
  input  WE,
  input  OE,
  input  reset,
  input  clock,
  output [7:0] Dout,
  output [7:0] Stored_bit
);

  one_bit_register one_bit_register_1 (
    .WE(WE), .Din(Din[7]), .OE(OE), .Reset(reset), .clock(clock), .Dout(Dout[7]), .Stored_bit(Stored_bit[7]));
  one_bit_register one_bit_register_2 (
    .WE(WE), .Din(Din[6]), .OE(OE), .Reset(reset), .clock(clock), .Dout(Dout[6]), .Stored_bit(Stored_bit[6]));
  one_bit_register one_bit_register_3 (
    .WE(WE), .Din(Din[5]), .OE(OE), .Reset(reset), .clock(clock), .Dout(Dout[5]), .Stored_bit(Stored_bit[5]));
  one_bit_register one_bit_register_4 (
    .WE(WE), .Din(Din[4]), .OE(OE), .Reset(reset), .clock(clock), .Dout(Dout[4]), .Stored_bit(Stored_bit[4]));
  one_bit_register one_bit_register_5 (
    .WE(WE), .Din(Din[3]), .OE(OE), .Reset(reset), .clock(clock), .Dout(Dout[3]), .Stored_bit(Stored_bit[3]));
  one_bit_register one_bit_register_6 (
    .WE(WE), .Din(Din[2]), .OE(OE), .Reset(reset), .clock(clock), .Dout(Dout[2]), .Stored_bit(Stored_bit[2]));
  one_bit_register one_bit_register_7 (
    .WE(WE), .Din(Din[1]), .OE(OE), .Reset(reset), .clock(clock), .Dout(Dout[1]), .Stored_bit(Stored_bit[1]));
  one_bit_register one_bit_register_8 (
    .WE(WE), .Din(Din[0]), .OE(OE), .Reset(reset), .clock(clock), .Dout(Dout[0]), .Stored_bit(Stored_bit[0]));
endmodule

module one_bit_register (
  input  clock,
  input  WE,
  input  Din,
  input  OE,
  input  Reset,
  output Dout,
  output Stored_bit
);

  wire and_1_out, and_2_out, not_1_out, or_1_out;

  not not_1 (not_1_out, WE);
  and and_1 (and_1_out, Stored_bit, not_1_out);
  and and_2 (and_2_out, WE, Din);
  or or_1 (or_1_out, and_1_out, and_2_out);
  D_Flip_Flop d_ff_1 (.D(or_1_out), .clk(clock), .Q(Stored_bit), .reset(Reset));  // open: Qn, preset
  assign Dout = OE ? Stored_bit : 1'bz;  // Controlled_Buffer controlled_buffer_1
endmodule

module sixteen_bit_register (
  input  [15:0] in_1,
  input  WE,
  input  OE,
  input  Reset,
  input  clock,
  output [15:0] out_6,
  output [15:0] out_7
);

  Eight_bit_register eight_bit_register_1 (
    .Din(in_1[15:8]), .OE(OE), .reset(Reset), .clock(clock), .WE(WE), .Stored_bit(out_7[15:8]),
    .Dout(out_6[15:8]));
  Eight_bit_register eight_bit_register_2 (
    .Din(in_1[7:0]), .OE(OE), .reset(Reset), .clock(clock), .WE(WE), .Stored_bit(out_7[7:0]),
    .Dout(out_6[7:0]));
endmodule
